# Fritzing sketch alarm_clock (saved by Fritzing 1.0.2b)
breadboards: 1

parts:
  Part1 = Arduino Uno (Rev3)
  U1 = 7-Segment-Display-4-Red [part_number=HS420561K package="7-Segment-4 [THT]"]
  R1 = Resistor [tolerance=±5% power=0.25W resistance=1k package=THT]
  R2 = Resistor [tolerance=±5% power=0.25W resistance=1k package=THT]
  R3 = Resistor [tolerance=±5% power=0.25W resistance=1k package=THT]
  R4 = Resistor [tolerance=±5% power=0.25W resistance=1k package=THT]
  S1 = Pushbutton [package="[THT]"]

nets:
  N1: Part1.D8, U1.pin_10
  N2: Part1.D9_PWM, U1.pin_11
  N3: Part1.D10_PWM/SS, R1.Pin_1
  N4: Part1.D11_PWM/MOSI, R2.Pin_1
  N5: Part1.D12/MISO, R3.Pin_1
  N6: Part1.D13/SCK, R4.Pin_1
  N7: Part1.GND, S1.Pin_1, S1.Pin_2
  N8: Part1.D0/RX, S1.Pin_3, S1.Pin_4
  N9: Part1.D2, U1.pin7
  N10: Part1.D3_PWM, U1.pin4
  N11: Part1.D4, U1.pin3
  N12: Part1.D5_PWM, U1.pin2
  N13: Part1.D6_PWM, U1.pin1
  N14: Part1.D7, U1.pin5
  N15: U1.pin6, R4.Pin_0
  N16: U1.pin8, R3.Pin_0
  N17: U1.pin_9, R2.Pin_0
  N18: U1.pin_12, R1.Pin_0

custom parts:
  7-Segment-Display-4-Red: 7-Segment Display 4 digits Red
