# Fritzing sketch arduino_i2c_example (saved by Fritzing 1.0.2b)

parts:
  Part1 = Arduino Uno (Rev3)
  Part2 = Arduino Uno (Rev3)

nets:
  N1: Part1.A4/SDA, Part2.A4/SDA
  N2: Part1.A5/SCL, Part2.A5/SCL
  GND: Part1.GND, Part2.GND
