# Fritzing sketch atmega328_standalone (saved by Fritzing 1.0.2b)
breadboards: 1

parts:
  U1 = atmega328 [package=dip]
  U2 = Voltage Regulator - 5V [package="TO220 [THT]"]
  VCC1 = Battery
  C1 = Electrolytic Capacitor [capacitance=10µF voltage=35V package="100 mil [THT, electrolytic]"]
  C2 = Electrolytic Capacitor [capacitance=10µF voltage=35V package="100 mil [THT, electrolytic]"]
  R1 = Resistor [tolerance=±5% power=0.25W resistance=10k package=THT]
  C3 = Ceramic Capacitor [capacitance=22pF voltage=35V package="100 mil [THT, multilayer]"]
  XTAL1 = CRYSTAL - kHz [frequency="16 Mhz"]
  C4 = Ceramic Capacitor [capacitance=22pF voltage=35V package="100 mil [THT, multilayer]"]
  R2 = Resistor [tolerance=±5% power=0.25W resistance=220 package=THT]
  LED1 = LED - 3mm [color="Red (633nm)" current=0.030A package="3 mm [THT]"]

nets:
  N1: U1.RESET, U1.VCC, U1.D13, U2.output_voltage, C2.+, R1.Pin_0, R1.Pin_1
  GND: U1.GND, U2.GND, VCC1.-, C1.-, C2.-, C3.1, C4.1, LED1.cathode
  N2: U1.XLAT1, C3.0, XTAL1.pin_0
  N3: U1.XLAT2, XTAL1.pin_1, C4.0
  N4: U1.D12, R2.Pin_0, R2.Pin_1, LED1.anode
  N5: U2.input_voltage, VCC1.+, C1.+
